# Fritzing sketch SmartMeter (saved by Fritzing 0.9.3b)

parts:
  WeMos_D1_Mini1 = WeMos D1 Mini
  IR-LED = LEDs [package=led10mm]
  Resistor = Resistor [tolerance=±5% resistance=220k package=THT]
  IR-Photoresistor = PHOTOCELL [package=photocell]

nets:
  N1: WeMos_D1_Mini1.5V, IR-Photoresistor.P$2
  N2: WeMos_D1_Mini1.A0, Resistor.Pin_1, IR-Photoresistor.P$1
  N3: WeMos_D1_Mini1.D2, IR-LED.A
  N4: WeMos_D1_Mini1.G, IR-LED.C, Resistor.Pin_0
